// Logisim project Project_Group3.circ as structural Verilog: 5 circuits, main circuit main
module main (
  input  [14:0] Data_In,
  input  [2:0] Rs,
  input  in_3,
  input  [2:0] Rd,
  input  [2:0] Rt,
  input  Clk,
  output [14:0] out_7,
  output [14:0] out_8
);

  wire demultiplexer_1_out0, demultiplexer_1_out1, demultiplexer_1_out2, demultiplexer_1_out3,
       demultiplexer_1_out4, demultiplexer_1_out5, demultiplexer_1_out6, demultiplexer_1_out7;
  wire [14:0] register_1_q, register_2_q, register_3_q, register_4_q, register_5_q, register_6_q,
       register_7_q, register_8_q;

  Demultiplexer #(.select(3)) demultiplexer_1 (
    .out0(demultiplexer_1_out0), .out1(demultiplexer_1_out1), .out2(demultiplexer_1_out2),
    .out3(demultiplexer_1_out3), .out4(demultiplexer_1_out4), .out5(demultiplexer_1_out5),
    .out6(demultiplexer_1_out6), .out7(demultiplexer_1_out7), .in(in_3), .sel(Rd));  // open: en
  Register #(.width(15)) register_1 (.D(Data_In), .en(demultiplexer_1_out0), .Q(register_1_q), .clk(Clk));  // open: clr
  Register #(.width(15)) register_2 (.D(Data_In), .en(demultiplexer_1_out1), .Q(register_2_q), .clk(Clk));  // open: clr
  Register #(.width(15)) register_3 (.D(Data_In), .en(demultiplexer_1_out2), .Q(register_3_q), .clk(Clk));  // open: clr
  Register #(.width(15)) register_4 (.D(Data_In), .en(demultiplexer_1_out3), .Q(register_4_q), .clk(Clk));  // open: clr
  Register #(.width(15)) register_5 (.D(Data_In), .en(demultiplexer_1_out4), .Q(register_5_q), .clk(Clk));  // open: clr
  Register #(.width(15)) register_6 (.D(Data_In), .en(demultiplexer_1_out5), .Q(register_6_q), .clk(Clk));  // open: clr
  Register #(.width(15)) register_7 (.D(Data_In), .en(demultiplexer_1_out6), .Q(register_7_q), .clk(Clk));  // open: clr
  Register #(.width(15)) register_8 (.D(Data_In), .en(demultiplexer_1_out7), .Q(register_8_q), .clk(Clk));  // open: clr
  Multiplexer #(.select(3), .width(15)) multiplexer_1 (
    .in0(register_1_q), .in1(register_2_q), .in2(register_3_q), .in3(register_4_q), .in4(register_5_q),
    .in5(register_6_q), .in6(register_7_q), .in7(register_8_q), .out(out_7), .sel(Rs));  // open: en
  Multiplexer #(.select(3), .width(15)) multiplexer_2 (
    .in0(register_1_q), .in1(register_2_q), .in2(register_3_q), .in3(register_4_q), .in4(register_5_q),
    .in5(register_6_q), .in6(register_7_q), .in7(register_8_q), .out(out_8), .sel(Rt));  // open: en
endmodule

module _15_bit_ALU (
  input  in_1,
  input  [14:0] A,
  input  [14:0] B,
  input  [1:0] in_4,
  output Zero,
  output [14:0] RESULT,
  output out_7
);

  wire [14:0] adder_1_out, multiplier_1_out, subtractor_1_out, xor_1_out;

  Adder #(.width(15)) adder_1 (.a(A), .b(B), .out(adder_1_out), .cin(in_1), .cout(out_7));
  Subtractor #(.width(15)) subtractor_1 (.a(A), .b(B), .out(subtractor_1_out));  // open: bin, bout
  Multiplier #(.width(15)) multiplier_1 (.a(A), .b(B), .out(multiplier_1_out));  // open: cin, cout
  assign xor_1_out = A ^ B;  // XOR_Gate xor_1, 15 bits wide
  Multiplexer #(.select(2), .width(15), .enable("false")) multiplexer_1 (
    .in0(adder_1_out), .in1(subtractor_1_out), .in2(multiplier_1_out), .in3(xor_1_out), .out(RESULT),
    .sel(in_4));
  nor nor_1 (Zero, RESULT[0], RESULT[1], RESULT[2], RESULT[3], RESULT[4], RESULT[5], RESULT[6], RESULT[7], RESULT[8], RESULT[9], RESULT[10], RESULT[11], RESULT[12], RESULT[13], RESULT[14]);
endmodule

// mem to reg
module control_unit (
  input  A,
  input  B,
  input  C,
  output regdst,
  output regwrite,
  output alusrc,
  output memread,
  output memwrite,
  output mem_to_reg,
  output Branch,
  output [1:0] Aluop
);

  wire not_1_out;

  not not_1 (not_1_out, A);
  not not_2 (regwrite, B);
  not not_3 (regdst, C);
  xor xor_1 (alusrc, B, C);
  and and_1 (memwrite, B, regdst);
  and and_2 (Branch, B, C);
  and and_3 (Aluop[1], regwrite, regdst);
  and and_4 (Aluop[0], B, C);
  and and_5 (memread, regwrite, C);

  assign mem_to_reg = C;
endmodule

module Datapath (
  input  in_1,
  input  sl,
  input  clr,
  output [2:0] Opcode,
  output [14:0] out_5,
  output [2:0] Rs,
  output [2:0] Rt,
  output [14:0] out_8,
  output [2:0] Rd,
  output [2:0] Function,
  output [14:0] out_11,
  output [14:0] out_12,
  output [14:0] out_13,
  output [5:0] Immediate,
  output [1:0] out_15,
  output [1:0] out_16
);

  wire ALU_zero, and_1_out, clock_1_out, control_unit_1_alusrc, control_unit_1_branch,
       control_unit_1_mem_to_reg, control_unit_1_memread, control_unit_1_memwrite, control_unit_1_regdst,
       control_unit_1_regwrite;
  wire [2:0] multiplexer_1_out;
  wire [14:0] adder_1_out, adder_2_out, multiplexer_3_out, ram_1_data, register_1_q, Register_2_out_8;

  Clock clock_1 (.out(clock_1_out));
  Register #(.width(15)) register_1 (.D(multiplexer_3_out), .Q(register_1_q), .clk(clock_1_out));  // open: en, clr
  control_unit control_unit_1 (
    .A(Opcode[2]), .B(Opcode[1]), .C(Opcode[0]), .regdst(control_unit_1_regdst),
    .regwrite(control_unit_1_regwrite), .alusrc(control_unit_1_alusrc), .memread(control_unit_1_memread),
    .memwrite(control_unit_1_memwrite), .mem_to_reg(control_unit_1_mem_to_reg),
    .Branch(control_unit_1_branch), .Aluop(out_16));
  Adder #(.width(15)) adder_1 (.a(register_1_q), .b(15'h1), .out(adder_1_out));  // open: cin, cout
  ROM #(.addrWidth(15), .dataWidth(15)) rom_1 (
    .addr(register_1_q), .data({Opcode, Rs, Immediate[5:3], Rd, Function}));  // open: sel
  Multiplexer #(.width(3), .enable("false")) multiplexer_1 (
    .in0(Rd), .in1(Immediate[5:3]), .out(multiplexer_1_out), .sel(control_unit_1_regdst));
  assign out_13 = {{9{1'b0}}, {Immediate[5:3], Function}};  // Bit_Extender bit_extender_1
  main Register_2 (
    .Data_In(out_11), .in_3(control_unit_1_regwrite), .Rd(multiplexer_1_out), .out_7(out_5), .Rs(Rs),
    .out_8(Register_2_out_8), .Rt(Immediate[5:3]), .Clk(clock_1_out));
  Multiplexer #(.width(15), .enable("false")) multiplexer_2 (
    .in0(Register_2_out_8), .in1(out_13), .out(out_8), .sel(control_unit_1_alusrc));
  Alucontrol alucontrol_1 (.AluControlInput(out_15), .AluOp(out_16), .Function(Function));
  _15_bit_ALU ALU (.in_1(in_1), .A(out_5), .B(out_8), .RESULT(out_12), .in_4(out_15), .Zero(ALU_zero));  // open: out_7
  Multiplexer #(.width(15), .enable("false")) multiplexer_3 (
    .in0(adder_1_out), .in1(adder_2_out), .out(multiplexer_3_out), .sel(and_1_out));
  and and_1 (and_1_out, ALU_zero, control_unit_1_branch);
  Adder #(.width(15)) adder_2 (.a(adder_1_out), .b(out_13), .out(adder_2_out));  // open: cin, cout
  RAM #(.addrWidth(15), .dataWidth(15), .bus("separate")) ram_1 (
    .addr(out_12), .din(Register_2_out_8), .data(ram_1_data), .str(control_unit_1_memwrite), .sel(sl),
    .clk(clock_1_out), .ld(control_unit_1_memread), .clr(clr));
  Multiplexer #(.width(15), .enable("false")) multiplexer_4 (
    .in0(out_12), .in1(ram_1_data), .out(out_11), .sel(control_unit_1_mem_to_reg));

  assign Immediate[2:0] = Function;
  assign Rt = Immediate[5:3];

  // Notes on the sheet:
  //   contents of rom_1 (hex, n*v repeats v):
  //   1011 1023 1235 0 0 882
  //   Read Data1
  //   Read Data 2
endmodule

// Alu cu
module Alucontrol (
  input  [1:0] AluOp,
  input  [2:0] Function,
  output [1:0] AluControlInput
);

  wire [1:0] multiplexer_1_out;

  Multiplexer #(.select(3), .width(2)) multiplexer_1 (
    .in0(2'b00), .in1(2'b01), .in2(2'b10), .in3(2'b11), .out(multiplexer_1_out), .sel(Function));  // open: in4, in5, in6, in7, en
  Multiplexer #(.select(2), .width(2)) multiplexer_2 (
    .in0(2'b00), .in1(2'b01), .in2(multiplexer_1_out), .out(AluControlInput), .sel(AluOp));  // open: in3, en
endmodule
